# Fritzing sketch tv_speaker_power (saved by Fritzing 0.9.3b)
breadboards: 1

parts:
  Uno = Arduino Uno (Rev3)
  Power_plug1 = Power plug
  Part1 = IR Receiver Breakout [package=PCB]
  LED1 = DUO LED RG [package="5 mm [THT]"]
  R1 = Resistor [tolerance=±5% resistance=220 package=THT]
  U1 = G3VM-61E1 [package=g3vm-61e1]
  U2 = G3VM-61E1 [package=g3vm-61e1]
  S1 = Round Pushbutton
  R2 = Resistor [tolerance=±5% resistance=10k package=THT]
  LED2 = LED - 3mm [color="Red (633nm)" package="3 mm [THT]"]
  R3 = Resistor [tolerance=±5% resistance=220 package=THT]

nets:
  N1: Uno.D2, S1.leg0, R2.Pin_0
  N2: Uno.D4, LED1.red_anode
  N3: Uno.D5_PWM, LED1.green_anode
  N4: Uno.D6_PWM, U1.P$6, U2.P$6
  N5: Uno.D7, Part1.OUT, R3.Pin_1
  5V: Uno.5V, Part1.VCC, U1.P$5, U2.P$4, S1.leg1, LED2.anode
  GND: Uno.GND, Power_plug1.GND, Part1.GND, R1.Pin_0, U1.P$4, U2.P$5, R2.Pin_1
  VIN: Uno.VIN, Power_plug1.VCC
  N6: LED1.common_cathode, R1.Pin_1
  N7: LED2.cathode, R3.Pin_0

notes:
  Relays are on boards that accept GPIO signals to trip relay
